# Fritzing sketch board (saved by Fritzing 0.9.3b)
stripboards: 1

parts:
  Raspberry_Pi2 = Raspberry Pi 2
  S7 = Round Pushbutton
  S8 = Round Pushbutton
  S9 = Round Pushbutton
  S17 = Round Pushbutton
  S18 = Round Pushbutton
  S19 = Round Pushbutton
  S20 = Round Pushbutton
  S21 = Round Pushbutton
  S22 = Round Pushbutton
  S23 = Round Pushbutton
  R16 = Resistor [tolerance=±5% resistance=10k package=THT]
  R18 = Resistor [tolerance=±5% resistance=10k package=THT]
  R19 = Resistor [tolerance=±5% resistance=10k package=THT]
  R20 = Resistor [tolerance=±5% resistance=10k package=THT]
  R21 = Resistor [tolerance=±5% resistance=10k package=THT]
  R22 = Resistor [tolerance=±5% resistance=10k package=THT]
  R23 = Resistor [tolerance=±5% resistance=10k package=THT]
  R24 = Resistor [tolerance=±5% resistance=10k package=THT]
  R25 = Resistor [tolerance=±5% resistance=10k package=THT]
  R26 = Resistor [tolerance=±5% resistance=10k package=THT]

nets:
  N1: Raspberry_Pi2.3v3, R16.Pin_0, R18.Pin_0, R19.Pin_0, R20.Pin_0, R21.Pin_0, R22.Pin_0, R23.Pin_0, R24.Pin_0, R25.Pin_0, R26.Pin_0
  N2: Raspberry_Pi2.GPIO13, S23.leg0, R16.Pin_1
  N3: Raspberry_Pi2.GPIO19, S22.leg0, R25.Pin_1
  N4: Raspberry_Pi2.GPIO26, Raspberry_Pi2.GPIO21, S20.leg0, S21.leg0, R23.Pin_1, R24.Pin_1
  N5: Raspberry_Pi2.GPIO20, S19.leg0, R22.Pin_1
  N6: Raspberry_Pi2.GPIO16, S18.leg0, R21.Pin_1
  N7: Raspberry_Pi2.GPIO12, S17.leg0, R20.Pin_1
  N8: Raspberry_Pi2.GPIO25, S9.leg0, R19.Pin_1
  N9: Raspberry_Pi2.GPIO24, S8.leg0, R18.Pin_1
  N10: Raspberry_Pi2.GPIO23, S7.leg0, R26.Pin_1
  N11: Raspberry_Pi2.GND, S7.leg1, S8.leg1, S9.leg1, S17.leg1, S18.leg1, S19.leg1, S20.leg1, S21.leg1, S22.leg1, S23.leg1
