# Fritzing sketch breadboard (saved by Fritzing 0.9.3b)
breadboards: 1

parts:
  S12 = Pushbutton [package="[THT]"]
  R15 = Resistor [tolerance=±5% resistance=10k package=THT]
  S16 = Pushbutton [package="[THT]"]
  R5 = Resistor [tolerance=±5% resistance=10k package=THT]
  R4 = Resistor [tolerance=±5% resistance=10k package=THT]
  R9 = Resistor [tolerance=±5% resistance=10k package=THT]
  R13 = Resistor [tolerance=±5% resistance=10k package=THT]
  S14 = Pushbutton [package="[THT]"]
  R14 = Resistor [tolerance=±5% resistance=10k package=THT]
  S11 = Pushbutton [package="[THT]"]
  S13 = Pushbutton [package="[THT]"]
  R10 = Resistor [tolerance=±5% resistance=10k package=THT]
  S4 = Pushbutton [package="[THT]"]
  S5 = Pushbutton [package="[THT]"]
  Raspberry_Pi1 = Raspberry Pi 2
  S3 = Pushbutton [package="[THT]"]
  R3 = Resistor [tolerance=±5% resistance=10k package=THT]
  R11 = Resistor [tolerance=±5% resistance=10k package=THT]
  S10 = Pushbutton [package="[THT]"]
  R12 = Resistor [tolerance=±5% resistance=10k package=THT]
  S15 = Pushbutton [package="[THT]"]

nets:
  N1: S12.Pin_1, S12.Pin_2, S16.Pin_1, S16.Pin_2, S14.Pin_1, S14.Pin_2, S11.Pin_1, S11.Pin_2, S13.Pin_1, S13.Pin_2, S4.Pin_1, S4.Pin_2, S5.Pin_1, S5.Pin_2, S3.Pin_1, S3.Pin_2, S10.Pin_1, S10.Pin_2, S15.Pin_1, S15.Pin_2
  N2: S12.Pin_3, S12.Pin_4, Raspberry_Pi1.ID_SC, R11.Pin_1
  N3: R15.Pin_0, R5.Pin_0, R4.Pin_0, R9.Pin_0, R13.Pin_0, R14.Pin_0, R10.Pin_0, Raspberry_Pi1.3v3, R3.Pin_0, R11.Pin_0, R12.Pin_0
  N4: R15.Pin_1, S16.Pin_3, S16.Pin_4, Raspberry_Pi1.GPIO21
  N5: R5.Pin_1, S5.Pin_3, S5.Pin_4, Raspberry_Pi1.GPIO25
  N6: R4.Pin_1, S4.Pin_3, S4.Pin_4, Raspberry_Pi1.GPIO24
  N7: R9.Pin_1, Raspberry_Pi1.GPIO8, S10.Pin_3, S10.Pin_4
  N8: R13.Pin_1, S14.Pin_3, S14.Pin_4, Raspberry_Pi1.GPIO16
  N9: R14.Pin_1, Raspberry_Pi1.GPIO20, S15.Pin_3, S15.Pin_4
  N10: S11.Pin_3, S11.Pin_4, R10.Pin_1, Raspberry_Pi1.GPIO7
  N11: S13.Pin_3, S13.Pin_4, Raspberry_Pi1.GPIO12, R12.Pin_1
  N12: Raspberry_Pi1.GPIO23, S3.Pin_3, S3.Pin_4, R3.Pin_1
